# Fritzing sketch Circuito_semaforo_protoboard (saved by Fritzing 0.9.6b)
breadboards: 1

parts:
  R1 = Resistor [tolerance=±5% power=0.25 resistance=220 package=THT]
  R2 = Resistor [tolerance=±5% power=0.25 resistance=220 package=THT]
  R3 = Resistor [tolerance=±5% power=0.25 resistance=220 package=THT]
  Componente1 = Arduino Uno (Rev3)
  LED1 = LED - 5mm [color="Red (633nm)" current=0.030 package="5 mm [THT]"]
  LED2 = LED - 5mm [color="Green (565nm)" current=0.030 package="5 mm [THT]"]
  LED3 = LED - 5mm [color="Yellow (595nm)" current=0.030 package="5 mm [THT]"]

nets:
  N1: R1.Pin_0, Componente1.D4
  N2: R1.Pin_1, LED2.anode
  N3: R2.Pin_0, Componente1.D7
  N4: R2.Pin_1, LED3.anode
  N5: R3.Pin_0, Componente1.D9_PWM
  N6: R3.Pin_1, LED1.anode
  N7: Componente1.GND, LED1.cathode, LED2.cathode, LED3.cathode
